// Logisim project LIB_Jednostava_CPU.circ as structural Verilog: 2 circuits, main circuit Jednostava16_CPU
module Jednostava16_CPU (
  input  [15:0] BUS_DATA_IN,
  input  CLK_EN,
  input  CLK,
  input  INTL,
  input  INT_0,
  input  INT_1,
  input  INT_2,
  input  INT_3,
  input  INT_4,
  input  INT_5,
  input  INT_6,
  input  INT_7,
  output [3:0] out_13,
  output [7:0] out_14,
  output [7:0] out_15,
  output [3:0] out_16,
  output [7:0] BUS_SCT,
  output [3:0] out_18,
  output [3:0] out_19,
  output [7:0] out_20,
  output [3:0] out_21,
  output [3:0] out_22,
  output [3:0] out_23,
  output [7:0] out_24,
  output [3:0] out_25,
  output [3:0] out_26,
  output [7:0] out_27,
  output [3:0] out_28,
  output [7:0] out_29,
  output [15:0] BUS_DATA_OUT,
  output [7:0] out_31,
  output [3:0] out_32,
  output [7:0] out_33,
  output [3:0] out_34,
  output W,
  output [3:0] out_36,
  output [3:0] out_37,
  output [3:0] out_38,
  output [3:0] out_39,
  output [15:0] BUS_ADR,
  output CLK_T8,
  output [3:0] out_42,
  output [3:0] out_43,
  output [3:0] out_44,
  output [3:0] out_45,
  output [3:0] out_46,
  output CLK_T16,
  output CLK_T1,
  output [3:0] out_49,
  output [3:0] out_50,
  output [3:0] out_51,
  output [3:0] out_52,
  output [3:0] out_53,
  output [3:0] out_54,
  output [3:0] out_55,
  output [3:0] out_56,
  output [3:0] out_57,
  output [3:0] out_58,
  output [3:0] out_59,
  output [3:0] out_60,
  output [3:0] out_61,
  output [3:0] out_62,
  output [3:0] out_63,
  output [3:0] out_64,
  output [3:0] out_65,
  output [3:0] out_66,
  output [3:0] out_67,
  output [3:0] out_68,
  output [3:0] out_69,
  output [3:0] out_70,
  output [3:0] out_71,
  output [3:0] out_72,
  output R,
  output [7:0] out_74,
  output [3:0] out_75,
  output INTM
);

  wire ACT_DV_H, ACT_DV_L, ACT_INT_E, ACT_INT_S, ACT_PF, ALU_ALU_HL_co, ALU_ALU_LH_co, ALU_ALU_LL_co,
       AND_C_q, AND_E_q, AND_G_q, AND_H_q, AND_I_q, CIN, CMP, CO, EQU_HH, EQU_HL, EQU_LH, EQU_LL, EXE, FETCH,
       FLG_CO, FLG_EQU, FLG_NEG, INPUT_GR, INPUT_PF, IR_OE, NOT_A_q, NOT_B_q, NOT_C_q, NOT_D_q, OPC_A,
       OPC_CMPR, OPC_DVR, OPC_INTC, OPC_PF, OPC_RF, OPC_SF, OR_D_q, OR_G_q, OR_I_q, OUTPUT_M, SRC_ADRD,
       SRC_DVR, SRC_INTB, SRC_PF, SRC_R, SRC_RF, SRC_SF, STEP_2, STEP_3, STEP_5, STEP_7, X_q;
  wire [0:0] CMPU_MUL_w;
  wire [1:0] BUS_ARGO, BUS_ARGS;
  wire [2:0] ALU_ALU_HH_f, SCU_CNT_q;
  wire [3:0] ALU_ALU_HL_f, ALU_ALU_LH_f, ALU_ALU_LL_f;
  wire [5:0] BUS_OP;
  wire [7:0] ALU_REG_A_H_o, ALU_REG_A_L_o, IEU_REG_I_H_o;
  wire [7:1] CMPU_REG_o;
  wire [15:0] BUS_DATA_IN_t, BUS_DATA_OUT_t;

  IC_74574 ALU_REG_A_L (.D(BUS_DATA_IN_t[7:0]), .CP(OPC_A), .OE(1'b0), .O(ALU_REG_A_L_o), .val(out_29));
  IC_74574 ALU_REG_A_H (.D(BUS_DATA_IN_t[15:8]), .CP(OPC_A), .OE(1'b0), .O(ALU_REG_A_H_o), .val(out_33));
  IC_74151 CMPU_MUL (
    .S({1'b1, BUS_ARGO}), .D0(1'b1), .D1(1'b1), .D2(1'b1), .D3(1'b1), .D4(FLG_NEG), .D5(FLG_CO),
    .D6(FLG_EQU), .D7(INTM), .EN(1'b0), .W(CMPU_MUL_w[0]));  // open: Y
  IC_74670 RF_FILE_LL (
    .RA(BUS_ARGS), .WA(BUS_ARGO), .WE(OPC_RF), .D(BUS_DATA_OUT_t[3:0]), .RE(SRC_RF), .val3(out_44),
    .val2(out_42), .Q(BUS_DATA_IN_t[3:0]), .val1(out_38), .val0(out_36));
  IC_74670 RF_FILE_LH (
    .RA(BUS_ARGS), .WA(BUS_ARGO), .WE(OPC_RF), .D(BUS_DATA_OUT_t[7:4]), .RE(SRC_RF), .val3(out_55),
    .val2(out_53), .Q(BUS_DATA_IN_t[7:4]), .val1(out_51), .val0(out_49));
  IC_74670 RF_FILE_HL (
    .RA(BUS_ARGS), .WA(BUS_ARGO), .WE(OPC_RF), .D(BUS_DATA_OUT_t[11:8]), .RE(SRC_RF), .val3(out_63),
    .val2(out_61), .Q(BUS_DATA_IN_t[11:8]), .val1(out_59), .val0(out_57));
  IC_74670 RF_FILE_HH (
    .RA(BUS_ARGS), .WA(BUS_ARGO), .WE(OPC_RF), .D(BUS_DATA_OUT_t[15:12]), .RE(SRC_RF), .val3(out_71),
    .val2(out_69), .Q(BUS_DATA_IN_t[15:12]), .val1(out_67), .val0(out_65));
  IC_74574 CMPU_REG (.D({{7{1'b1}}, CMPU_MUL_w[0]}), .CP(OPC_CMPR), .OE(OPC_PF), .O({CMPU_REG_o, CMP}), .val(out_74));
  IC_74181 ALU_ALU_LL (
    .CIN(CIN), .M(BUS_OP[4]), .A(BUS_DATA_IN_t[3:0]), .S(BUS_OP[3:0]), .B(ALU_REG_A_L_o[3:0]), .AEQB(EQU_LL),
    .CO(ALU_ALU_LL_co), .val(out_21), .F(ALU_ALU_LL_f));  // open: G, P
  IC_74181 ALU_ALU_LH (
    .CIN(ALU_ALU_LL_co), .M(BUS_OP[4]), .A(BUS_DATA_IN_t[7:4]), .S(BUS_OP[3:0]), .B(ALU_REG_A_L_o[7:4]),
    .AEQB(EQU_LH), .CO(ALU_ALU_LH_co), .val(out_28), .F(ALU_ALU_LH_f));  // open: G, P
  IC_74181 ALU_ALU_HL (
    .CIN(ALU_ALU_LH_co), .M(BUS_OP[4]), .A(BUS_DATA_IN_t[11:8]), .S(BUS_OP[3:0]), .B(ALU_REG_A_H_o[3:0]),
    .AEQB(EQU_HL), .CO(ALU_ALU_HL_co), .val(out_32), .F(ALU_ALU_HL_f));  // open: G, P
  IC_74181 ALU_ALU_HH (
    .CIN(ALU_ALU_HL_co), .M(BUS_OP[4]), .A(BUS_DATA_IN_t[15:12]), .S(BUS_OP[3:0]), .B(ALU_REG_A_H_o[7:4]),
    .AEQB(EQU_HH), .CO(CO), .val(out_34), .F({FLG_NEG, ALU_ALU_HH_f}));  // open: G, P
  IC_74161 IC_CNT (
    .LD(1'b0), .D(4'b1111), .CLK(ACT_INT_E), .CLR(ACT_INT_S), .ENT(1'b1), .ENP(1'b1), .val(out_75), .CO(INTM));  // open: Q
  IC_74574 ALU_REG_G_L (
    .D({ALU_ALU_LH_f, ALU_ALU_LL_f}), .CP(INPUT_GR), .OE(1'b0), .O(BUS_DATA_OUT_t[7:0]), .val(out_27));
  IC_74574 ALU_REG_G_H (
    .D({FLG_NEG, ALU_ALU_HH_f, ALU_ALU_HL_f}), .CP(INPUT_GR), .OE(1'b0), .O(BUS_DATA_OUT_t[15:8]),
    .val(out_31));
  IC_74670 PF_FILE_LL (
    .RA(BUS_ARGS), .WA(BUS_ARGO), .WE(ACT_PF), .D(BUS_DATA_OUT_t[3:0]), .RE(1'b0), .val3(out_45),
    .val2(out_43), .Q(BUS_ADR[3:0]), .val1(out_39), .val0(out_37));
  IC_74670 PF_FILE_LH (
    .RA(BUS_ARGS), .WA(BUS_ARGO), .WE(ACT_PF), .D(BUS_DATA_OUT_t[7:4]), .RE(1'b0), .val3(out_56),
    .val2(out_54), .Q(BUS_ADR[7:4]), .val1(out_52), .val0(out_50));
  IC_74670 PF_FILE_HL (
    .RA(BUS_ARGS), .WA(BUS_ARGO), .WE(ACT_PF), .D(BUS_DATA_OUT_t[11:8]), .RE(1'b0), .val3(out_64),
    .val2(out_62), .Q(BUS_ADR[11:8]), .val1(out_60), .val0(out_58));
  IC_74670 PF_FILE_HH (
    .RA(BUS_ARGS), .WA(BUS_ARGO), .WE(ACT_PF), .D(BUS_DATA_OUT_t[15:12]), .RE(1'b0), .val3(out_72),
    .val2(out_70), .Q(BUS_ADR[15:12]), .val1(out_68), .val0(out_66));
  IC_74541 PF_BUF_L (.I(BUS_ADR[7:0]), .OE1(SRC_PF), .OE2(1'b0), .Y(BUS_DATA_IN_t[7:0]));
  IC_74541 PF_BUF_H (.I(BUS_ADR[15:8]), .OE1(SRC_PF), .OE2(1'b0), .Y(BUS_DATA_IN_t[15:8]));
  IC_74541 IC_BUF_INT (
    .I({INT_7, INT_6, INT_5, INT_4, INT_3, INT_2, INT_1, INT_0}), .OE1(SRC_INTB), .OE2(1'b0),
    .Y(BUS_DATA_IN_t[7:0]));
  IC_74574 IEU_REG_I_L (.D(BUS_DATA_IN_t[7:0]), .CP(FETCH), .OE(IR_OE), .O({BUS_ARGS, BUS_OP}), .val(out_14));
  IC_74574 IEU_REG_I_H (
    .D(BUS_DATA_IN_t[15:8]), .CP(FETCH), .OE(IR_OE), .O({IEU_REG_I_H_o[7:5], BUS_ARGO, IEU_REG_I_H_o[2:0]}),
    .val(out_24));
  RESISTOR resistor_1 (.R_IN(INTM), .R_OUT_B(IR_OE), .R_OUT_A(BUS_ARGS[1]));
  RESISTOR resistor_2 (.R_IN(INTM), .R_OUT_B(IR_OE), .R_OUT_A(BUS_ARGO[1]));
  Pull_Resistor pull_resistor_1 (.node({IEU_REG_I_H_o[7:5], BUS_ARGO, IEU_REG_I_H_o[2:0], BUS_ARGS, BUS_OP}));
  IC_7406 NOT_A (.A(OPC_DVR), .Q(NOT_A_q));
  IC_7408 AND_C (.A(EQU_LL), .B(EQU_LH), .Q(AND_C_q));
  IC_7408 AND_E (.A(EQU_HL), .B(EQU_HH), .Q(AND_E_q));
  IC_7406 NOT_B (.A(OPC_INTC), .Q(NOT_B_q));
  IC_7432 AND_H (.A(INTL), .B(STEP_7), .Q(AND_H_q));
  IC_7408 OR_D (.A(CLK_T1), .B(FETCH), .Q(OR_D_q));
  IC_7408 OR_G (.A(STEP_3), .B(INPUT_PF), .Q(OR_G_q));
  IC_7408 AND_A (.A(BUS_ARGO[0]), .B(NOT_A_q), .Q(ACT_DV_L));
  IC_7408 AND_B (.A(NOT_A_q), .B(BUS_ARGO[1]), .Q(ACT_DV_H));
  IC_7408 AND_D (.A(AND_C_q), .B(AND_E_q), .Q(FLG_EQU));
  IC_7408 AND_F (.A(BUS_ARGO[0]), .B(NOT_B_q), .Q(ACT_INT_E));
  IC_7400 AND_G (.A(NOT_B_q), .B(BUS_ARGO[1]), .Q(AND_G_q));
  IC_7400 OR_E (.A(OR_D_q), .B(STEP_2), .Q(SRC_R));
  IC_7400 OR_I (.A(BUS_OP[5]), .B(CO), .Q(OR_I_q));
  IC_74574 IEU_DV_L (.D({BUS_ARGS, BUS_OP}), .CP(ACT_DV_L), .OE(SRC_DVR), .O(BUS_DATA_IN_t[7:0]), .val(out_15));
  IC_74574 IEU_DV_H (.D({BUS_ARGS, BUS_OP}), .CP(ACT_DV_H), .OE(SRC_DVR), .O(BUS_DATA_IN_t[15:8]), .val(out_20));
  IC_74138 IEU_DCD_SRC (
    .EN3(1'b0), .D(IEU_REG_I_H_o[2:0]), .EN1(1'b1), .EN2(SRC_R), .Y0(SRC_PF), .Y2(SRC_RF), .Y3(SRC_SF),
    .Y5(SRC_DVR), .Y6(SRC_ADRD), .Y7(SRC_INTB));  // open: Y1, Y4
  IC_74138 IEU_DCD_OPC (
    .EN3(1'b0), .D(IEU_REG_I_H_o[7:5]), .EN1(1'b1), .EN2(EXE), .Y0(OPC_PF), .Y1(OPC_A), .Y2(OPC_RF),
    .Y3(OPC_SF), .Y4(OPC_CMPR), .Y5(OPC_DVR), .Y6(W), .Y7(OPC_INTC));
  IC_7408 OR_C (.A(AND_G_q), .B(AND_H_q), .Q(ACT_INT_S));
  IC_7406 NOT_C (.A(SRC_R), .Q(NOT_C_q));
  IC_7432 AND_I (.A(SRC_R), .B(SRC_ADRD), .Q(AND_I_q));
  IC_7406 NOT_F (.A(OR_I_q), .Q(CIN));
  IC_7406 NOT_E (.A(CO), .Q(FLG_CO));
  IC_7408 OR_F (.A(NOT_C_q), .B(AND_I_q), .Q(R));
  IC_7400 OR_H (.A(NOT_C_q), .B(OR_G_q), .Q(IR_OE));
  IC_7432 X (.A(1'b1), .B(1'b1), .Q(X_q));
  IC_7408 OR_A (.A(STEP_3), .B(STEP_5), .Q(INPUT_GR));
  IC_7408 OR_B (.A(CMP), .B(INPUT_PF), .Q(ACT_PF));
  IC_7406 NOT_D (.A(SRC_ADRD), .Q(NOT_D_q));
  IC_7432 AND_J (.A(NOT_D_q), .B(IR_OE), .Q(OUTPUT_M));
  // NoConnect on X_q
  IC_74161 SCU_CNT (
    .LD(1'b1), .D(4'b1111), .CLK(CLK), .CLR(1'b1), .ENT(CLK_EN), .ENP(1'b1), .val(out_46),
    .Q({CLK_T8, SCU_CNT_q}), .CO(CLK_T16));
  IC_74670 SF_FILE_L (
    .RA(BUS_ARGS), .WA(BUS_ARGO), .WE(OPC_SF), .D(BUS_DATA_OUT_t[3:0]), .RE(1'b0), .val3(out_19),
    .val2(out_18), .Q(BUS_SCT[3:0]), .val1(out_16), .val0(out_13));
  IC_74670 SF_FILE_H (
    .RA(BUS_ARGS), .WA(BUS_ARGO), .WE(OPC_SF), .D(BUS_DATA_OUT_t[7:4]), .RE(1'b0), .val3(out_26),
    .val2(out_25), .Q(BUS_SCT[7:4]), .val1(out_23), .val0(out_22));
  IC_74541 IOU_BUF_OUT_L (.I(BUS_DATA_OUT_t[7:0]), .OE1(OUTPUT_M), .OE2(1'b0), .Y(BUS_DATA_OUT[7:0]));
  IC_74541 IOU_BUF_OUT_H (.I(BUS_DATA_OUT_t[15:8]), .OE1(OUTPUT_M), .OE2(1'b0), .Y(BUS_DATA_OUT[15:8]));
  IC_74541 IOU_BUF_IN_L (.I(BUS_DATA_IN[7:0]), .OE1(R), .OE2(1'b0), .Y(BUS_DATA_IN_t[7:0]));
  IC_74541 IOU_BUF_IN_H (.I(BUS_DATA_IN[15:8]), .OE1(R), .OE2(1'b0), .Y(BUS_DATA_IN_t[15:8]));
  IC_74138 SCU_DCD (
    .EN3(1'b0), .D(SCU_CNT_q), .EN1(1'b1), .EN2(1'b0), .Y0(CLK_T1), .Y1(FETCH), .Y2(STEP_2), .Y3(STEP_3),
    .Y4(INPUT_PF), .Y5(STEP_5), .Y6(EXE), .Y7(STEP_7));
  IC_74541 SF_BUF (.I(BUS_SCT), .OE1(SRC_SF), .OE2(1'b0), .Y(BUS_DATA_IN_t[7:0]));

  // Other names for the same wires on the sheet: FLG_INTM = INTM; INPUT_M = R; OPC_ADRD = W; STEP_0 = CLK_T1;
  //   STEP_1 = FETCH; STEP_4 = INPUT_PF; STEP_6 = EXE

  // Notes on the sheet:
  //   ALU (8 IC)
  //   RFU (4 IC)
  //   CMPU (2 IC)
  //   PFU (6 IC)
  //   ICU (2 IC)
  //   IEU (6 IC)
  //   CMBL (6 IC)
  //   SFU (3 IC)
  //   IOU (4 IC)
  //   SCU (2 IC)
  //   43 IC
  //   2 MIPS
  //   PC MEM 64KB
  //   AP MEM 16MB
  //   Jednostava16
  //   28.10.2026.
  //   Ivan Jonjic (IJPantic on github)
endmodule

module Jednostava8_CPU (
  input  [7:0] BUS_DATA_IN,
  input  CLK_EN,
  input  CLK,
  input  INTL,
  output [3:0] out_5,
  output [7:0] out_6,
  output [7:0] out_7,
  output [3:0] out_8,
  output [3:0] BUS_SCT,
  output [3:0] out_10,
  output [3:0] out_11,
  output [7:0] out_12,
  output [3:0] out_13,
  output [7:0] out_14,
  output [7:0] out_15,
  output [3:0] out_16,
  output [7:0] BUS_DATA_OUT,
  output W,
  output CLK_T8,
  output [3:0] out_20,
  output CLK_T16,
  output CLK_T1,
  output [3:0] out_23,
  output [3:0] out_24,
  output [3:0] out_25,
  output [3:0] out_26,
  output [7:0] BUS_ADR,
  output [3:0] out_28,
  output [3:0] out_29,
  output [3:0] out_30,
  output [3:0] out_31,
  output [3:0] out_32,
  output [3:0] out_33,
  output [3:0] out_34,
  output [3:0] out_35,
  output [3:0] out_36,
  output [3:0] out_37,
  output [3:0] out_38,
  output [3:0] out_39,
  output R,
  output [7:0] out_41,
  output [3:0] out_42,
  output INTM
);

  wire ACT_DV, ACT_INT_E, ACT_INT_S, ACT_PF, ALU_ALU_L_co, AND_D_q, AND_E_q, AND_F_q, CIN, CMP, CO, EQU_LH,
       EQU_LL, EXE, FETCH_H, FETCH_L, FLG_CO, FLG_EQU, FLG_NEG, ic_7400_1_q, INPUT_GR, INPUT_PF_A,
       INPUT_PF_B, IR_OE, NOT_A_q, NOT_B_q, NOT_C_q, NOT_D_q, OPC_A, OPC_CMPR, OPC_DVR, OPC_INTC, OPC_PF,
       OPC_RF, OPC_SF, OR_A_q, OR_C_q, OR_F_q, OR_G_q, OR_I_q, OR_J_q, OR_M_q, OR_N_q, OR_O_q, OUTPUT_M,
       SRC_ADRD, SRC_DVR, SRC_INTB, SRC_PF, SRC_R, SRC_RF, SRC_SF, STEP_2, STEP_3, STEP_5, STEP_6, STEP_7,
       STEP_8, STEP_10, STEP_11, STEP_13, STEP_15, X_q;
  wire [0:0] CMPU_MUL_w;
  wire [1:0] BUS_ARGO, BUS_ARGS;
  wire [2:0] ALU_ALU_H_f, SCU_CNT_q;
  wire [3:0] ALU_ALU_L_f;
  wire [5:0] BUS_OP;
  wire [7:0] ALU_REG_A_o, BUS_DATA_IN_t, BUS_DATA_OUT_t, IEU_REG_I_H_o;
  wire [7:1] CMPU_REG_o;

  IC_74574 ALU_REG_A (.D(BUS_DATA_IN_t), .CP(OPC_A), .OE(1'b0), .O(ALU_REG_A_o), .val(out_14));
  IC_74151 CMPU_MUL (
    .S({1'b1, BUS_ARGO}), .D0(1'b1), .D1(1'b1), .D2(1'b1), .D3(1'b1), .D4(FLG_NEG), .D5(FLG_CO),
    .D6(FLG_EQU), .D7(INTM), .EN(1'b0), .W(CMPU_MUL_w[0]));  // open: Y
  IC_74670 RF_FILE_L (
    .RA(BUS_ARGS), .WA(BUS_ARGO), .WE(OPC_RF), .D(BUS_DATA_OUT_t[3:0]), .RE(SRC_RF), .val3(out_30),
    .val2(out_28), .Q(BUS_DATA_IN_t[3:0]), .val1(out_25), .val0(out_23));
  IC_74670 RF_FILE_H (
    .RA(BUS_ARGS), .WA(BUS_ARGS), .WE(OPC_RF), .D(BUS_DATA_OUT_t[7:4]), .RE(SRC_RF), .val3(out_38),
    .val2(out_36), .Q(BUS_DATA_IN_t[7:4]), .val1(out_34), .val0(out_32));
  IC_74574 CMPU_REG (.D({{7{1'b1}}, CMPU_MUL_w[0]}), .CP(OPC_CMPR), .OE(OPC_PF), .O({CMPU_REG_o, CMP}), .val(out_41));
  IC_74181 ALU_ALU_L (
    .CIN(CIN), .M(BUS_OP[4]), .A(BUS_DATA_IN_t[3:0]), .S(BUS_OP[3:0]), .B(ALU_REG_A_o[3:0]), .AEQB(EQU_LL),
    .CO(ALU_ALU_L_co), .val(out_13), .F(ALU_ALU_L_f));  // open: G, P
  IC_74181 ALU_ALU_H (
    .CIN(ALU_ALU_L_co), .M(BUS_OP[4]), .A(BUS_DATA_IN_t[7:4]), .S(BUS_OP[3:0]), .B(ALU_REG_A_o[7:4]),
    .AEQB(EQU_LH), .CO(CO), .val(out_16), .F({FLG_NEG, ALU_ALU_H_f}));  // open: G, P
  IC_74574 ALU_REG_G (
    .D({FLG_NEG, ALU_ALU_H_f, ALU_ALU_L_f}), .CP(INPUT_GR), .OE(1'b0), .O(BUS_DATA_OUT_t), .val(out_15));
  IC_74670 PF_FILE_L (
    .RA(BUS_ARGS), .WA(BUS_ARGO), .WE(ACT_PF), .D(BUS_DATA_OUT_t[3:0]), .RE(1'b0), .val3(out_31),
    .val2(out_29), .Q(BUS_ADR[3:0]), .val1(out_26), .val0(out_24));
  IC_74670 PF_FILE_H (
    .RA(BUS_ARGS), .WA(BUS_ARGS), .WE(ACT_PF), .D(BUS_DATA_OUT_t[7:4]), .RE(1'b0), .val3(out_39),
    .val2(out_37), .Q(BUS_ADR[7:4]), .val1(out_35), .val0(out_33));
  IC_74161 IC_CNT (
    .LD(1'b0), .D(4'b1111), .CLK(ACT_INT_E), .CLR(ACT_INT_S), .ENT(1'b1), .ENP(1'b1), .val(out_42), .CO(INTM));  // open: Q
  IC_74541 PF_BUF (.I(BUS_ADR), .OE1(SRC_PF), .OE2(1'b0), .Y(BUS_DATA_IN_t));
  IC_7408 OR_A (.A(STEP_3), .B(STEP_5), .Q(OR_A_q));
  IC_7408 OR_C (.A(INPUT_PF_A), .B(INPUT_PF_B), .Q(OR_C_q));
  IC_7406 NOT_B (.A(OPC_INTC), .Q(NOT_B_q));
  IC_7432 AND_E (.A(INTL), .B(STEP_7), .Q(AND_E_q));
  IC_7408 OR_F (.A(CLK_T1), .B(FETCH_L), .Q(OR_F_q));
  IC_7408 OR_I (.A(STEP_8), .B(FETCH_H), .Q(OR_I_q));
  IC_7408 OR_M (.A(STEP_3), .B(INPUT_PF_A), .Q(OR_M_q));
  IC_7408 OR_O (.A(STEP_11), .B(INPUT_PF_B), .Q(OR_O_q));
  IC_74574 IEU_REG_I_L (.D(BUS_DATA_IN_t), .CP(FETCH_L), .OE(IR_OE), .O({BUS_ARGS, BUS_OP}), .val(out_6));
  IC_74574 IEU_REG_I_H (
    .D(BUS_DATA_IN_t), .CP(FETCH_H), .OE(IR_OE), .O({IEU_REG_I_H_o[7:5], BUS_ARGO, IEU_REG_I_H_o[2:0]}),
    .val(out_12));
  RESISTOR resistor_1 (.R_IN(INTM), .R_OUT_B(IR_OE), .R_OUT_A(BUS_ARGS[1]));
  RESISTOR resistor_2 (.R_IN(INTM), .R_OUT_B(IR_OE), .R_OUT_A(BUS_ARGO[1]));
  IC_7408 OR_B (.A(OR_A_q), .B(STEP_11), .Q(INPUT_GR));
  IC_7408 OR_D (.A(OR_C_q), .B(CMP), .Q(ACT_PF));
  IC_7408 AND_C (.A(BUS_ARGO[0]), .B(NOT_B_q), .Q(ACT_INT_E));
  IC_7400 AND_D (.A(NOT_B_q), .B(BUS_ARGO[1]), .Q(AND_D_q));
  IC_7408 OR_G (.A(OR_F_q), .B(STEP_2), .Q(OR_G_q));
  IC_7408 OR_J (.A(OR_I_q), .B(STEP_10), .Q(OR_J_q));
  IC_7408 OR_N (.A(OR_M_q), .B(OR_O_q), .Q(OR_N_q));
  Pull_Resistor pull_resistor_1 (.node({IEU_REG_I_H_o[7:5], BUS_ARGO, IEU_REG_I_H_o[2:0], BUS_ARGS, BUS_OP}));
  IC_7408 OR_E (.A(AND_D_q), .B(AND_E_q), .Q(ACT_INT_S));
  IC_7400 OR_H (.A(OR_G_q), .B(OR_J_q), .Q(SRC_R));
  IC_7406 NOT_C (.A(SRC_R), .Q(NOT_C_q));
  IC_7432 AND_F (.A(SRC_R), .B(SRC_ADRD), .Q(AND_F_q));
  IC_74574 IEU_DV (.D({BUS_ARGS, BUS_OP}), .CP(ACT_DV), .OE(SRC_DVR), .O(BUS_DATA_IN_t), .val(out_7));
  IC_74138 IEU_DCD_SRC (
    .EN3(1'b0), .D(IEU_REG_I_H_o[2:0]), .EN1(1'b1), .EN2(SRC_R), .Y0(SRC_PF), .Y2(SRC_RF), .Y3(SRC_SF),
    .Y5(SRC_DVR), .Y6(SRC_ADRD), .Y7(SRC_INTB));  // open: Y1, Y4
  IC_74138 IEU_DCD_OPC (
    .EN3(1'b0), .D(IEU_REG_I_H_o[7:5]), .EN1(1'b1), .EN2(EXE), .Y0(OPC_PF), .Y1(OPC_A), .Y2(OPC_RF),
    .Y3(OPC_SF), .Y4(OPC_CMPR), .Y5(OPC_DVR), .Y6(W), .Y7(OPC_INTC));
  IC_7406 NOT_A (.A(OPC_DVR), .Q(NOT_A_q));
  IC_7408 OR_K (.A(NOT_C_q), .B(AND_F_q), .Q(R));
  IC_7406 NOT_D (.A(SRC_ADRD), .Q(NOT_D_q));
  IC_7400 OR_L (.A(NOT_C_q), .B(OR_N_q), .Q(IR_OE));
  IC_7400 ic_7400_1 (.A(BUS_OP[5]), .B(CO), .Q(ic_7400_1_q));
  IC_7408 AND_A (.A(EQU_LL), .B(EQU_LH), .Q(FLG_EQU));
  IC_7408 AND_B (.A(BUS_ARGO[0]), .B(NOT_A_q), .Q(ACT_DV));
  IC_7432 X (.A(1'b1), .B(1'b1), .Q(X_q));
  IC_7432 AND_G (.A(NOT_D_q), .B(IR_OE), .Q(OUTPUT_M));
  IC_7406 NOT_F (.A(ic_7400_1_q), .Q(CIN));
  IC_7406 NOT_E (.A(CO), .Q(FLG_CO));
  // NoConnect on X_q
  IC_74161 SCU_CNT (
    .LD(1'b1), .D(4'b1111), .CLK(CLK), .CLR(1'b1), .ENT(CLK_EN), .ENP(1'b1), .val(out_20),
    .Q({CLK_T8, SCU_CNT_q}), .CO(CLK_T16));
  IC_74670 SF_FILE_L (
    .RA(BUS_ARGS), .WA(BUS_ARGO), .WE(OPC_SF), .D(BUS_DATA_OUT_t[3:0]), .RE(1'b0), .val3(out_11),
    .val2(out_10), .Q(BUS_SCT), .val1(out_8), .val0(out_5));
  IC_74541 IOU_BUF_OUT (.I(BUS_DATA_OUT_t), .OE1(OUTPUT_M), .OE2(1'b0), .Y(BUS_DATA_OUT));
  IC_74541 IOU_BUF_IN (.I(BUS_DATA_IN), .OE1(R), .OE2(1'b0), .Y(BUS_DATA_IN_t));
  IC_74138 SCU_DCD_L (
    .EN3(1'b0), .D(SCU_CNT_q), .EN1(1'b1), .EN2(CLK_T8), .Y0(CLK_T1), .Y1(FETCH_L), .Y2(STEP_2), .Y3(STEP_3),
    .Y4(INPUT_PF_A), .Y5(STEP_5), .Y6(STEP_6), .Y7(STEP_7));
  IC_74138 SCU_DCD_H (
    .EN3(1'b0), .D(SCU_CNT_q), .EN1(CLK_T8), .EN2(1'b0), .Y0(STEP_8), .Y1(FETCH_H), .Y2(STEP_10),
    .Y3(STEP_11), .Y4(INPUT_PF_B), .Y5(STEP_13), .Y6(EXE), .Y7(STEP_15));
  IC_74541 SF_BUF (.I({4'b1111, BUS_SCT}), .OE1(SRC_SF), .OE2(1'b0), .Y(BUS_DATA_IN_t));

  // Other names for the same wires on the sheet: FLG_INTM = INTM; INPUT_M = R; OPC_ADRD = W; STEP_0 = CLK_T1;
  //   STEP_1 = FETCH_L; STEP_4 = INPUT_PF_A; STEP_9 = FETCH_H; STEP_12 = INPUT_PF_B; STEP_14 = EXE

  // Notes on the sheet:
  //   ALU (4 IC)
  //   RFU (2 IC)
  //   CMPU (2 IC)
  //   PFU (3 IC)
  //   ICU (1 IC)
  //   IEU (5 IC)
  //   CMBL (7 IC)
  //   SCU (3 IC)
  //   31 IC
  //   1 MIPS
  //   SFU (2 IC)
  //   IOU (2 IC)
  //   PC MEM 256B
  //   AP MEM 4KB
  //   Jednostava8
  //   28.10.2026.
  //   Ivan Jonjic (IJPantic on github)
endmodule
