// Logisim project Semafor.circ as structural Verilog: 1 circuit, main circuit main
module main (
  output [3:0] out_1,
  output [3:0] out_2,
  output [3:0] out_3,
  output [3:0] out_4,
  output [3:0] out_5,
  output [3:0] out_6,
  output [3:0] out_7,
  output [3:0] out_8,
  output [3:0] out_9,
  output [3:0] out_10,
  output [3:0] out_11,
  output [3:0] out_12,
  output [3:0] out_13,
  output [3:0] out_14,
  output [3:0] out_15,
  output [3:0] out_16,
  output [3:0] out_17,
  output [3:0] out_18,
  output [3:0] out_19,
  output [3:0] out_20,
  output [7:0] out_21,
  output [3:0] out_22,
  output [3:0] out_23,
  output [7:0] out_24,
  output [7:0] out_25,
  output [7:0] out_26,
  output [7:0] out_27,
  output [3:0] out_28,
  output [3:0] out_29,
  output [7:0] out_30,
  output [7:0] out_31,
  output [7:0] IO_OUTPUT
);

  wire button_1_out, CE_IO, CE_ROM, clk_out, ic_7432_1_q, jednostava8_cpu_1_r, jednostava8_cpu_1_w;
  wire [3:0] jednostava8_cpu_1_bus_sct;
  wire [7:0] inst_mem_A_data, jednostava8_cpu_1_bus_adr, jednostava8_cpu_1_bus_data_out;

  Clock clk (.out(clk_out));
  Jednostava8_CPU jednostava8_cpu_1 (
    .CLK_EN(1'b1), .CLK(clk_out), .INTL(button_1_out), .BUS_DATA_IN(jednostava8_cpu_1_bus_data_out),
    .out_38(out_23), .out_10(out_25), .out_5(out_26), .out_6(out_24), .out_42(out_22),
    .R(jednostava8_cpu_1_r), .W(jednostava8_cpu_1_w), .out_7(out_1), .out_8(out_6), .out_11(out_11),
    .out_12(out_16), .BUS_DATA_OUT(jednostava8_cpu_1_bus_data_out), .BUS_SCT(jednostava8_cpu_1_bus_sct),
    .out_18(out_5), .out_20(out_10), .out_24(out_15), .out_26(out_20), .out_28(out_4), .out_30(out_9),
    .out_32(out_14), .out_34(out_19), .out_16(out_27), .out_9(out_29), .out_15(out_28), .out_37(out_21),
    .out_19(out_3), .out_21(out_8), .out_25(out_13), .out_27(out_18), .out_29(out_2), .out_31(out_7),
    .out_33(out_12), .out_35(out_17), .out_14(out_30), .BUS_ADR(jednostava8_cpu_1_bus_adr));  // open: CLK_T16, CLK_T8, CLK_T1, INTM
  IC_74138 sct_dcd (
    .EN3(1'b0), .D(jednostava8_cpu_1_bus_sct[2:0]), .EN1(1'b1), .EN2(jednostava8_cpu_1_bus_sct[3]),
    .Y0(CE_ROM), .Y1(CE_IO));  // open: Y2, Y3, Y4, Y5, Y6, Y7
  ROM inst_mem_A (.addr(jednostava8_cpu_1_bus_adr), .data(inst_mem_A_data));
  IC_7432 ic_7432_1 (.A(CE_IO), .B(jednostava8_cpu_1_w), .Q(ic_7432_1_q));
  Button #(.press("passive")) button_1 (.out(button_1_out));
  IC_74574 output_reg (.D(jednostava8_cpu_1_bus_data_out), .CP(ic_7432_1_q), .OE(1'b0), .O(IO_OUTPUT), .val(out_31));
  LED led_1 (.in(IO_OUTPUT[0]));
  LED led_2 (.in(IO_OUTPUT[1]));
  LED led_3 (.in(IO_OUTPUT[2]));
  LED led_4 (.in(IO_OUTPUT[3]));
  LED led_5 (.in(IO_OUTPUT[4]));
  IC_74541 ic_74541_1 (
    .I(inst_mem_A_data), .OE1(jednostava8_cpu_1_r), .OE2(CE_ROM), .Y(jednostava8_cpu_1_bus_data_out));

  // Notes on the sheet:
  //   contents of inst_mem_A (hex, n*v repeats v):
  //   0 e8 1c 78 1c 40 20 c2 0 e0 0 e0 0 e0 0 e0 0 e0 0 e0 0 e0 0 e0
  //   VOZILA
  //   PJEŠACI
endmodule
